// Logisim project 1part.circ as structural Verilog: 1 circuit, main circuit main
module main (
  input  in_1,
  input  in_2,
  input  in_3,
  input  in_4,
  input  in_5,
  input  in_6,
  input  in_7,
  input  in_8,
  input  in_9,
  input  in_10,
  input  in_11,
  input  in_12,
  input  in_13,
  input  in_14,
  input  in_15,
  input  in_16,
  output out_17,
  output out_18,
  output out_19,
  output out_20,
  output out_21,
  output out_22,
  output out_23,
  output out_24,
  output out_25
);

  wire and_1_out, and_2_out, and_3_out, and_4_out, and_5_out, and_6_out, and_7_out, and_8_out, and_9_out,
       and_10_out, and_11_out, and_12_out, and_13_out, and_14_out, and_15_out, and_16_out, and_17_out,
       and_18_out, and_19_out, and_20_out, and_21_out, and_22_out, and_23_out, and_24_out, and_25_out,
       and_26_out, and_27_out, and_28_out, and_29_out, and_30_out, and_31_out, and_32_out, and_33_out,
       and_34_out, and_35_out, and_36_out, and_37_out, and_38_out, and_39_out, and_40_out, and_41_out,
       and_42_out, and_43_out, and_44_out, and_45_out, and_46_out, and_47_out, and_48_out, and_49_out,
       and_50_out, and_51_out, and_52_out, and_53_out, and_54_out, and_55_out, and_56_out, not_1_out,
       not_2_out, not_3_out, not_4_out, not_5_out, not_6_out, not_7_out, not_8_out, not_9_out, not_10_out,
       not_11_out, not_12_out, not_13_out, not_14_out, not_15_out, not_16_out, not_17_out, not_18_out,
       not_19_out, not_20_out, not_21_out, not_22_out, not_23_out, not_24_out, or_4_out, or_6_out, or_7_out,
       or_9_out, or_11_out, or_13_out, or_15_out;

  not not_1 (not_1_out, in_1);
  not not_2 (not_2_out, in_10);
  not not_3 (not_3_out, or_4_out);
  and and_1 (and_1_out, in_1, in_10);
  and and_2 (and_2_out, in_1, or_4_out);
  and and_3 (and_3_out, in_10, or_4_out);
  and and_4 (and_4_out, in_1, not_2_out, not_3_out);
  and and_5 (and_5_out, in_10, not_1_out, not_3_out);
  and and_6 (and_6_out, or_4_out, not_1_out, not_2_out);
  and and_7 (and_7_out, in_1, in_10, or_4_out);
  or or_1 (out_17, and_1_out, and_2_out, and_3_out);
  or or_2 (out_18, and_4_out, and_5_out, and_6_out, and_7_out);
  not not_4 (not_4_out, in_2);
  not not_5 (not_5_out, in_11);
  not not_6 (not_6_out, or_6_out);
  and and_8 (and_8_out, in_2, in_11);
  and and_9 (and_9_out, in_2, or_6_out);
  and and_10 (and_10_out, in_11, or_6_out);
  and and_11 (and_11_out, in_2, not_5_out, not_6_out);
  and and_12 (and_12_out, in_11, not_4_out, not_6_out);
  and and_13 (and_13_out, or_6_out, not_4_out, not_5_out);
  and and_14 (and_14_out, in_2, in_11, or_6_out);
  or or_3 (out_19, and_11_out, and_12_out, and_13_out, and_14_out);
  or or_4 (or_4_out, and_8_out, and_9_out, and_10_out);
  not not_7 (not_7_out, in_3);
  not not_8 (not_8_out, in_12);
  not not_9 (not_9_out, or_7_out);
  and and_15 (and_15_out, in_3, in_12);
  and and_16 (and_16_out, in_3, or_7_out);
  and and_17 (and_17_out, in_12, or_7_out);
  and and_18 (and_18_out, in_3, not_8_out, not_9_out);
  and and_19 (and_19_out, in_12, not_7_out, not_9_out);
  or or_5 (out_20, and_18_out, and_19_out, and_20_out, and_21_out);
  and and_20 (and_20_out, or_7_out, not_7_out, not_8_out);
  and and_21 (and_21_out, in_3, in_12, or_7_out);
  or or_6 (or_6_out, and_15_out, and_16_out, and_17_out);
  not not_10 (not_10_out, in_4);
  not not_11 (not_11_out, in_13);
  not not_12 (not_12_out, or_9_out);
  and and_22 (and_22_out, in_4, in_13);
  and and_23 (and_23_out, in_4, or_9_out);
  and and_24 (and_24_out, in_13, or_9_out);
  and and_25 (and_25_out, in_4, not_11_out, not_12_out);
  and and_26 (and_26_out, in_13, not_10_out, not_12_out);
  and and_27 (and_27_out, or_9_out, not_10_out, not_11_out);
  and and_28 (and_28_out, in_4, in_13, or_9_out);
  or or_7 (or_7_out, and_22_out, and_23_out, and_24_out);
  or or_8 (out_21, and_25_out, and_26_out, and_27_out, and_28_out);
  not not_13 (not_13_out, in_5);
  not not_14 (not_14_out, in_14);
  not not_15 (not_15_out, or_11_out);
  and and_29 (and_29_out, in_5, in_14);
  and and_30 (and_30_out, in_5, or_11_out);
  and and_31 (and_31_out, in_14, or_11_out);
  and and_32 (and_32_out, in_5, not_14_out, not_15_out);
  and and_33 (and_33_out, in_14, not_13_out, not_15_out);
  and and_34 (and_34_out, or_11_out, not_13_out, not_14_out);
  and and_35 (and_35_out, in_5, in_14, or_11_out);
  or or_9 (or_9_out, and_29_out, and_30_out, and_31_out);
  or or_10 (out_22, and_32_out, and_33_out, and_34_out, and_35_out);
  not not_16 (not_16_out, in_6);
  not not_17 (not_17_out, in_15);
  not not_18 (not_18_out, or_13_out);
  and and_36 (and_36_out, in_6, in_15);
  and and_37 (and_37_out, in_6, or_13_out);
  and and_38 (and_38_out, in_15, or_13_out);
  and and_39 (and_39_out, in_6, not_17_out, not_18_out);
  and and_40 (and_40_out, in_15, not_16_out, not_18_out);
  and and_41 (and_41_out, or_13_out, not_16_out, not_17_out);
  and and_42 (and_42_out, in_6, in_15, or_13_out);
  or or_11 (or_11_out, and_36_out, and_37_out, and_38_out);
  or or_12 (out_23, and_39_out, and_40_out, and_41_out, and_42_out);
  not not_19 (not_19_out, in_16);
  not not_20 (not_20_out, or_15_out);
  not not_21 (not_21_out, in_7);
  and and_43 (and_43_out, in_7, in_16);
  and and_44 (and_44_out, in_7, or_15_out);
  and and_45 (and_45_out, in_16, or_15_out);
  and and_46 (and_46_out, in_7, not_19_out, not_20_out);
  and and_47 (and_47_out, in_16, not_21_out, not_20_out);
  and and_48 (and_48_out, or_15_out, not_21_out, not_19_out);
  and and_49 (and_49_out, in_7, in_16, or_15_out);
  or or_13 (or_13_out, and_43_out, and_44_out, and_45_out);
  or or_14 (out_24, and_46_out, and_47_out, and_48_out, and_49_out);
  not not_22 (not_22_out, in_9);
  not not_23 (not_23_out, 1'b0);
  not not_24 (not_24_out, in_8);
  and and_50 (and_50_out, in_8, in_9);
  and and_51 (and_51_out, in_8, 1'b0);
  and and_52 (and_52_out, in_9, 1'b0);
  and and_53 (and_53_out, in_8, not_22_out, not_23_out);
  and and_54 (and_54_out, in_9, not_24_out, not_23_out);
  and and_55 (and_55_out, 1'b0, not_24_out, not_22_out);
  and and_56 (and_56_out, in_8, in_9, 1'b0);
  or or_15 (or_15_out, and_50_out, and_51_out, and_52_out);
  or or_16 (out_25, and_53_out, and_54_out, and_55_out, and_56_out);

  // Notes on the sheet:
  //   in_10: initial=0x1
  //   in_11: initial=0x1
  //   in_12: initial=0x1
  //   in_13: initial=0x1
  //   in_14: initial=0x1
  //   in_15: initial=0x1
  //   in_16: initial=0x1
  //   in_9: initial=0x1
endmodule
