// Logisim project 2part.circ as structural Verilog: 1 circuit, main circuit main
module main (
  input  A,
  input  B,
  input  C,
  input  D,
  output Y3,
  output Y2,
  output Y1,
  output Y0
);

  wire and_1_out, and_2_out, and_3_out, and_4_out, and_5_out, and_6_out, not_1_out, not_2_out, not_3_out,
       not_4_out;

  and and_1 (and_1_out, C, not_1_out);
  not not_1 (not_1_out, A);
  not not_2 (not_2_out, B);
  and and_2 (and_2_out, not_1_out, not_2_out);
  not not_3 (not_3_out, C);
  not not_4 (not_4_out, D);
  and and_3 (and_3_out, not_4_out, C);
  and and_4 (and_4_out, B, C, D);
  and and_5 (and_5_out, B, D);
  and and_6 (and_6_out, not_3_out, A);
  or or_1 (Y3, and_4_out, and_2_out);
  or or_2 (Y2, and_3_out, and_2_out);
  or or_3 (Y1, and_5_out, and_6_out, and_1_out);

  assign Y0 = D;
endmodule
