// Logisim project 3part.circ as structural Verilog: 1 circuit, main circuit main
module main (
);

  wire and_1_out, clock_1_out, t_ff_2_q, t_ff_3_q;

  T_Flip_Flop t_ff_1 (.T(and_1_out), .clk(clock_1_out));  // open: Q, Qn, reset, preset
  and and_1 (and_1_out, t_ff_3_q, t_ff_2_q);
  Clock clock_1 (.out(clock_1_out));
  T_Flip_Flop t_ff_2 (.T(t_ff_3_q), .clk(clock_1_out), .Q(t_ff_2_q));  // open: Qn, reset, preset
  T_Flip_Flop t_ff_3 (.T(1'b1), .clk(clock_1_out), .Q(t_ff_3_q));  // open: Qn, reset, preset
endmodule
