// Logisim project dop_task_RAM.circ as structural Verilog: 1 circuit, main circuit main
module main (
  input  A2,
  input  A1,
  input  A0,
  input  WE,
  input  D3,
  input  D2,
  input  D1,
  input  D0,
  output Q3,
  output Q2,
  output Q1,
  output Q0
);

  wire and_1_out, and_2_out, and_3_out, and_4_out, and_5_out, and_6_out, and_7_out, and_8_out, and_9_out,
       and_10_out, and_11_out, and_12_out, and_13_out, and_14_out, and_15_out, and_16_out, and_17_out,
       and_18_out, and_19_out, and_20_out, and_21_out, and_22_out, and_23_out, and_24_out, and_25_out,
       and_26_out, and_27_out, and_28_out, and_29_out, and_30_out, and_31_out, and_32_out, and_33_out,
       and_34_out, and_35_out, and_36_out, and_37_out, and_38_out, and_39_out, and_40_out, and_41_out,
       and_42_out, and_43_out, and_44_out, and_45_out, and_46_out, and_47_out, and_48_out, CLK_out,
       not_1_out, not_2_out, not_3_out;
  wire [3:0] R0_q, R1_q, R2_q, R3_q, R4_q, R5_q, R6_q, R7_q;

  Clock CLK (.out(CLK_out));
  not not_1 (not_1_out, A2);
  not not_2 (not_2_out, A1);
  not not_3 (not_3_out, A0);
  and and_1 (and_1_out, not_1_out, not_2_out, not_3_out);
  and and_2 (and_2_out, not_1_out, not_2_out, A0);
  and and_3 (and_3_out, not_1_out, A1, not_3_out);
  and and_4 (and_4_out, not_1_out, A1, A0);
  Register #(.width(4)) R0 (.D({D3, D2, D1, D0}), .en(and_5_out), .clk(CLK_out), .Q(R0_q));  // open: clr
  and and_5 (and_5_out, and_1_out, WE);
  Register #(.width(4)) R1 (.D({D3, D2, D1, D0}), .en(and_6_out), .clk(CLK_out), .Q(R1_q));  // open: clr
  and and_6 (and_6_out, and_2_out, WE);
  Register #(.width(4)) R2 (.D({D3, D2, D1, D0}), .en(and_7_out), .clk(CLK_out), .Q(R2_q));  // open: clr
  and and_7 (and_7_out, and_3_out, WE);
  Register #(.width(4)) R3 (.D({D3, D2, D1, D0}), .en(and_8_out), .clk(CLK_out), .Q(R3_q));  // open: clr
  and and_8 (and_8_out, and_4_out, WE);
  Register #(.width(4)) R4 (.D({D3, D2, D1, D0}), .en(and_9_out), .clk(CLK_out), .Q(R4_q));  // open: clr
  and and_9 (and_9_out, and_13_out, WE);
  Register #(.width(4)) R5 (.D({D3, D2, D1, D0}), .en(and_10_out), .clk(CLK_out), .Q(R5_q));  // open: clr
  and and_10 (and_10_out, and_14_out, WE);
  Register #(.width(4)) R6 (.D({D3, D2, D1, D0}), .en(and_11_out), .clk(CLK_out), .Q(R6_q));  // open: clr
  and and_11 (and_11_out, and_15_out, WE);
  Register #(.width(4)) R7 (.D({D3, D2, D1, D0}), .en(and_12_out), .clk(CLK_out), .Q(R7_q));  // open: clr
  and and_12 (and_12_out, and_16_out, WE);
  and and_13 (and_13_out, A2, not_2_out, A0);
  and and_14 (and_14_out, A2, not_2_out, A0);
  and and_15 (and_15_out, A2, A1, not_3_out);
  and and_16 (and_16_out, A0, A1, A2);
  and and_17 (and_17_out, and_1_out, R0_q[0]);
  and and_18 (and_18_out, and_2_out, R1_q[0]);
  and and_19 (and_19_out, and_3_out, R2_q[0]);
  and and_20 (and_20_out, and_4_out, R3_q[0]);
  and and_21 (and_21_out, and_13_out, R4_q[0]);
  and and_22 (and_22_out, and_14_out, R5_q[0]);
  and and_23 (and_23_out, and_15_out, R6_q[0]);
  and and_24 (and_24_out, and_16_out, R7_q[0]);
  and and_25 (and_25_out, and_1_out, R0_q[1]);
  and and_26 (and_26_out, and_2_out, R1_q[1]);
  and and_27 (and_27_out, and_3_out, R2_q[1]);
  and and_28 (and_28_out, and_4_out, R3_q[1]);
  and and_29 (and_29_out, and_13_out, R4_q[1]);
  and and_30 (and_30_out, and_14_out, R5_q[1]);
  and and_31 (and_31_out, and_15_out, R6_q[1]);
  and and_32 (and_32_out, and_16_out, R7_q[1]);
  and and_33 (and_33_out, and_1_out, R0_q[2]);
  and and_34 (and_34_out, and_2_out, R1_q[2]);
  and and_35 (and_35_out, and_3_out, R2_q[2]);
  and and_36 (and_36_out, and_4_out, R3_q[2]);
  and and_37 (and_37_out, and_13_out, R4_q[2]);
  and and_38 (and_38_out, and_14_out, R5_q[2]);
  and and_39 (and_39_out, and_15_out, R6_q[2]);
  and and_40 (and_40_out, and_16_out, R7_q[2]);
  and and_41 (and_41_out, and_1_out, R0_q[3]);
  and and_42 (and_42_out, and_2_out, R1_q[3]);
  and and_43 (and_43_out, and_3_out, R2_q[3]);
  and and_44 (and_44_out, and_4_out, R3_q[3]);
  and and_45 (and_45_out, and_13_out, R4_q[3]);
  and and_46 (and_46_out, and_14_out, R5_q[3]);
  and and_47 (and_47_out, and_15_out, R6_q[3]);
  and and_48 (and_48_out, and_16_out, R7_q[3]);
  or or_1 (Q0, and_17_out, and_18_out, and_19_out, and_20_out, and_21_out, and_22_out, and_23_out, and_24_out);
  or or_2 (Q1, and_25_out, and_26_out, and_27_out, and_28_out, and_29_out, and_30_out, and_31_out, and_32_out);
  or or_3 (Q2, and_33_out, and_34_out, and_35_out, and_36_out, and_37_out, and_38_out, and_39_out, and_40_out);
  or or_4 (Q3, and_41_out, and_42_out, and_43_out, and_44_out, and_45_out, and_46_out, and_47_out, and_48_out);
endmodule
